# Fritzing sketch home_remote_controler_mini_schematics (saved by Fritzing 1.0.5)
circuit board: 7.28938cm x 4.35533cm
breadboards: 1

parts:
  U2 = Optocoupler [package=THT]
  R5 = Resistor [tolerance=±5% power=0.25W resistance=220 package=THT]
  R7 = Resistor [tolerance=±5% power=0.25W resistance=1k package=THT]
  R1 = Photocell (LDR) [power=0.25W dark_resistance_@0.01lx=300kΩ light_resistance_@100lx=400Ω luminance=10lx package=THT]
  R4 = Resistor [tolerance=±5% power=0.25W resistance=1k package=THT]
  R8 = TRIMPOT [maximum_resistance=10kΩ knob_status=50% power=0.5W package=trim_pot_pth]
  DHT1 = DHT11 Humitidy and Temperature Sensor (3 pins)
  Part1 = Arduino Nano (Rev3.0)
  LCD1 = LCD screen

nets:
  N1: U2.Pin_1, R4.Pin_0
  GND: U2.Pin_2, R7.Pin_1, R8.CW, DHT1.Gnd, Part1.GND, LCD1.VSS, LCD1.R/W, LCD1.LED-
  N2: R5.Pin_0, LCD1.LED+
  5V: R5.Pin_1, R1.pin_1, R8.CCW, DHT1.Signal, Part1.5V, LCD1.VDD
  N3: R7.Pin_0, R1.pin_0, Part1.A0
  N4: R4.Pin_1, Part1.D12/MISO
  N5: R8.WIPER, LCD1.V0
  N6: DHT1.Plus, Part1.D11/MOSI
  N7: Part1.D5, LCD1.DB7
  N8: Part1.D6, LCD1.DB6
  N9: Part1.D7, LCD1.DB5
  N10: Part1.D8, LCD1.DB4
  N11: Part1.D9, LCD1.E
  N12: Part1.D10, LCD1.RS

notes:
  DHT 11 PINS: S Vin GND
  Left to Right
  5V 1 - 1.2A

custom parts:
  DHT11 Humitidy and Temperature Sensor (3 pins): DHT11 Humidity and Temperature Sensor (3 pins).
